# Fritzing sketch Electronic Circuit (saved by Fritzing 0.9.4)
breadboards: 1

parts:
  Componente1 = Arduino Uno (Rev3) - ICSP
  Componente2 = Bluetooth HC-05 Macho
  J1 = Basic Servo
  J2 = Basic Servo
  J3 = Basic Servo
  J4 = Basic Servo
  J5 = Basic Servo

nets:
  GND: Componente1.GND, Componente2.GND, J1.gnd, J2.gnd, J3.gnd, J4.gnd, J5.gnd
  N1: Componente1.D8, Componente2.RXD
  N2: Componente1.D9_PWM, J4.pulse
  N3: Componente1.D10_PWM/SS, J5.pulse
  N4: Componente1.D3_PWM, J1.pulse
  N5: Componente1.D5_PWM, J2.pulse
  N6: Componente1.D6_PWM, J3.pulse
  N7: Componente1.D7, Componente2.TXD
  3V3: Componente1.3V3, Componente2.VCC
  VCC: Componente1.5V, J1.vcc, J2.vcc, J3.vcc, J4.vcc, J5.vcc
